# Fritzing sketch openSmartCountryGPRS (saved by Fritzing 0.9.2b)
circuit board: 4.04447cm x 5.32059cm
breadboards: 1

parts:
  SIM800L = SIM800L [package=THT]
  ANT1 = Antenna
  U3 = LIPO-2000mAh [package=lipo-2000]
  MOISTURE_SENSOR = mystery part, 3 pins [chip_label="Moisture Sensor"]
  DHT11 = Humidity and Temperature Sensor RHT03
  R1 = Resistor [tolerance=±5% resistance=220 package="0805 [SMD]"]
  LIGHT_SENSOR = Photocell (LDR) [package=THT]
  R3 = Resistor [tolerance=±5% resistance=220 package=THT]
  RAIN_SENSOR = mystery part, 4 pins [chip_label="Rain sensor"]
  Parte1 = Arduino Uno (Rev3)

nets (from the breadboard view):
  GND: SIM800L.GND, U3.-, MOISTURE_SENSOR.pin1, DHT11.GND_1, R3.Pin_0, RAIN_SENSOR.pin2, Parte1.GND
  N1: SIM800L.TXD, Parte1.D10_PWM/SS
  N2: SIM800L.RXD, Parte1.D11_PWM/MOSI
  N3: SIM800L.RST, Parte1.D12/MISO
  N4: SIM800L.VCC, U3.+
  N5: SIM800L.NET, ANT1.antenna_lead
  N6: MOISTURE_SENSOR.pin2, Parte1.D5_PWM
  N7: MOISTURE_SENSOR.pin3, Parte1.A2
  N8: DHT11.Vcc, R1.Pin_1, Parte1.D3_PWM
  N9: DHT11.Data-signal, R1.Pin_0, Parte1.D4
  N10: LIGHT_SENSOR.pin_0, R3.Pin_1, Parte1.A0
  N11: LIGHT_SENSOR.pin_1, Parte1.D9_PWM
  N12: RAIN_SENSOR.pin1, Parte1.D6_PWM
  N13: RAIN_SENSOR.pin3, Parte1.D7
  N14: RAIN_SENSOR.pin4, Parte1.A1
